# Fritzing sketch simon-fritz (saved by Fritzing 0.9.4)
breadboards: 2

parts:
  LED1 = LED - 5mm [color="Red (633nm)" package="5 mm [THT]"]
  LED2 = LED - 5mm [color="Yellow (595nm)" package="5 mm [THT]"]  # not connected
  LED3 = LED - 5mm [color="Blue (430nm)" package="5 mm [THT]"]
  LED4 = LED - 5mm [color="Green (555nm)" package="5 mm [THT]"]
  R6 = Resistor [tolerance=±20% resistance=10k package="0402 [SMD]"]
  R7 = Resistor [tolerance=±20% resistance=10k package="0402 [SMD]"]
  R8 = Resistor [tolerance=±20% resistance=10k package="0402 [SMD]"]
  R9 = Resistor [tolerance=±20% resistance=10k package="0402 [SMD]"]
  Raspberry_Pi_1 = Raspberry Pi 3 [part_number=RPI-3-V1.2]
  S1 = Pushbutton [package="[THT]"]
  S2 = Pushbutton [package="[THT]"]
  S3 = Pushbutton [package="[THT]"]
  S4 = Pushbutton [package="[THT]"]

nets:
  N1: LED1.cathode, R7.Pin_1
  N2: LED1.anode, Raspberry_Pi_1.GPIO23
  N3: LED3.cathode, R9.Pin_1
  N4: LED3.anode, Raspberry_Pi_1.GPIO22
  N5: LED4.cathode, R8.Pin_1
  N6: LED4.anode, Raspberry_Pi_1.GPIO27
  N7: R6.Pin_0, R7.Pin_0, R8.Pin_0, R9.Pin_0, Raspberry_Pi_1.GND, S1.Pin_3, S1.Pin_4, S2.Pin_3, S2.Pin_4, S3.Pin_3, S3.Pin_4, S4.Pin_3, S4.Pin_4
  N8: Raspberry_Pi_1.GPIO2, S1.Pin_1, S1.Pin_2
  N9: Raspberry_Pi_1.GPIO3, S3.Pin_1, S3.Pin_2
  N10: Raspberry_Pi_1.GPIO26, S4.Pin_1, S4.Pin_2
  N11: Raspberry_Pi_1.GPIO14, S2.Pin_1, S2.Pin_2
